# Fritzing sketch push button xbee (saved by Fritzing 0.9.3b)
breadboards: 1

parts:
  U1 = XBEE-1 [package=xbee-1]
  U2 = XBEE-1 [package=xbee-1]
  Part1 = Arduino Mega ADK (Rev3)
  Part2 = Arduino Uno (Rev3)
  S1 = Pushbutton [package="[THT]"]
  J1 = Piezo Speaker
  R1 = Resistor [tolerance=±5% resistance=220 package="1206 [SMD]"]
  D1 = LTE-302 [package=lte-302]
  D2 = LTE-302 [package=lte-302]

nets:
  VDD: U1.VDD, U2.VDD
  N1: U1.DOUT, Part1.D19/RX1
  N2: U1.DIN, Part1.D18/TX1
  GND: U1.GND, U2.GND, Part2.GND, J1.pin2, R1.Pin_1, D1.C
  N3: U2.DOUT, Part2.D4
  N4: U2.DIN, Part2.D5_PWM
  N5: Part1.GND, D2.C
  N6: Part1.D10_PWM, D2.A
  N7: Part1.D8_PWM, J1.pin1
  N8: Part2.D10_PWM/SS, D1.A
  N9: Part2.D2, S1.Pin_1, S1.Pin_2, R1.Pin_0
  N10: S1.Pin_3, S1.Pin_4

notes:
  ROUTER XBEE Connects to Passive Buzzer
  Corridinator XBEE
  5 Vcc
  3.3 Vcc
